// Digital circuit CPU.dig as structural Verilog
module CPU (
  input  in_11,
  input  in_17,
  input  in_18,
  input  CLK_RAW,
  output [31:0] x8_s0_fp,
  output [31:0] x9_s1,
  output [31:0] x10_a0,
  output [31:0] PC,
  output [31:0] ADDR,
  output [31:0] Instr,
  output [7:0] Dout,
  output [5:0] Step,
  output [7:0] Substep,
  output [7:0] Dval,
  output [16:0] out_12,
  output [15:0] out_13,
  output [31:0] A,
  output [31:0] B,
  output [31:0] Result,
  output [31:0] out_19,
  output [11:0] CSR_Address,
  output [31:0] x11_a1,
  output [31:0] x4_tp,
  output [31:0] x5_t0,
  output [31:0] x6_t1,
  output [31:0] x7_t2,
  output [31:0] x1_ra,
  output [31:0] x2_sp,
  output [31:0] x3_gp,
  output [31:0] x12_a2,
  output [31:0] x13_a3,
  output [31:0] x14_a4,
  output [31:0] x15_a5,
  output [5:0] out_34
);

  wire ADDR_CLK, ADDR_IN, ADDR_LATCH, ALU_A, ALU_AUX, ALU_B, ALU_N, alu_shift_step_1_nsh_output,
       alu_shift_step_1_sh_loadlen, alu_shift_step_1_sh_reset, and_1_out, B_INSTR, B_RUN, B_STEP, B_STOP,
       B_SUBSTEP, BUS_CLK, BUS_EN, BUT_STOP, CLK, clock_1_lastsubstep, comparator_1_eq, comparator_1_gt,
       comparator_1_lt, comparator_2_eq, CSR_ADDR_LATCH, CSR_IN, CSR_IN_LATCH, CSR_OUT, CSR_OUT_LATCH,
       d_ff_1_q, d_ff_3_q, hef4557b_1_q, ImmB, ImmCSR, ImmI, ImmJ, ImmS, ImmU, IRQ_OP, IRQ_OP_SnP, LASTSTEP,
       LEN8, MEM_IN, MEM_OUT, MEPC_OUT, MTVEC_OUT, multiplexer_1_out, nADDR_PE, nALU_RESET, nand_1_out, nCLK,
       nMEM_OE, nMEM_WE, nOPDONE, not_1_out, nPC_CNT_PE, nREG_IN_EN, nRESET, nS_EXT, nSTEPDONE, OP_IMM_LATCH,
       OP_IN, OP_IN_MUX, OP_LATCH, opcode_1_p21, or_1_out, PC_IN, PC_IN_LATCH, PC_OUT, PC_OUT_SnP, REG_IN,
       RESET, ROM_SEL, RS1, RSA, RSB, Running;
  wire [0:0] LEN;
  wire [1:0] ALU_A_MUX, REG_IN_MUX;
  wire [2:0] ALU_B_MUX, ALU_OP;
  wire [3:0] RSD;
  wire [7:0] ROM_DATA, ROM_DIN;
  wire [15:0] ROM_ADDR;
  wire [31:27] MicroCode_d;

  Register_view register_view_1 (
    .BUS_CLK(BUS_CLK), .nREG_IN_EN(nREG_IN_EN), .REG_IN(REG_IN), .RSD(RSD), .x1_ra(x1_ra), .x2_sp(x2_sp),
    .x3_gp(x3_gp), .x4_tp(x4_tp), .x5_t0(x5_t0), .x6_t1(x6_t1), .x7_t2(x7_t2), .x8_s0_fp(x8_s0_fp),
    .x9_s1(x9_s1), .x10_a0(x10_a0), .x11_a1(x11_a1), .x12_a2(x12_a2), .x13_a3(x13_a3), .x14_a4(x14_a4),
    .x15_a5(x15_a5));
  nand nand_1 (nand_1_out, PC_OUT_SnP, OP_IN_MUX);
  Multiplexer multiplexer_1 (.sel(out_12[13]), .in_0(RS1), .in_1(ImmCSR), .out(multiplexer_1_out));
  Comparator #(.Bits(32)) comparator_1 (
    .a(x3_gp), .b(32'h1), .gt(comparator_1_gt), .eq(comparator_1_eq), .lt(comparator_1_lt));
  LED led_1 (.in(Running));
  LED led_2 (.in(not_1_out));
  not not_1 (not_1_out, Running);
  Button #(.activeLow("true")) Stop (.out(BUT_STOP));
  Button #(.activeLow("true")) Run (.out(B_RUN));
  Button #(.activeLow("true")) One_Instruction (.out(B_INSTR));
  Button #(.activeLow("true")) One_Step (.out(B_STEP));
  Button #(.activeLow("true")) One_Substep (.out(B_SUBSTEP));
  LED led_3 (.in(comparator_1_gt));
  LED led_4 (.in(comparator_1_eq));
  PullDown pulldown_1 (.out(CSR_IN));
  CSR csr_1 (
    .CLK(BUS_CLK), .INA(multiplexer_1_out), .INB(CSR_IN), .CSR_FUNC(out_12[12:11]), .ADDR_IN(ImmI),
    .ADDR_LATCH(CSR_ADDR_LATCH), .nRESET(nRESET), .NEW_VAL(CSR_OUT), .ADDR(CSR_Address));
  Interrupt_Controller interrupt_controller_1 (
    .BUS_CLK(BUS_CLK), .MEPC_IN(PC_OUT), .nMEPC_IN_EN(nand_1_out), .IRQ_OP_SnP(IRQ_OP_SnP),
    .MTVEC_SnP(in_18), .LASTSTEP(LASTSTEP), .IRQ(in_17), .OP_LATCH(OP_LATCH), .RESET(RESET), .nRESET(nRESET),
    .MEPC_OUT(MEPC_OUT), .IRQ_OP(IRQ_OP), .MTVEC_OUT(MTVEC_OUT), .IRQ_OP_FETCH(OP_IN_MUX), .MEPC(out_19));
  and and_1 (and_1_out, nRESET, nOPDONE);
  D_FF #(.Default(1)) d_ff_1 (.D(comparator_1_lt), .C(~nOPDONE), .Q(d_ff_1_q));  // open: nQ
  D_FF_AS d_ff_as_1 (.Set(~1'b1), .D(1'b1), .C(ADDR_LATCH), .Clr(~and_1_out), .Q(IRQ_OP_SnP));  // open: nQ
  and and_2 (B_STOP, d_ff_1_q, BUT_STOP);
  DebugShift32 debugshift32_1 (.CLK(BUS_CLK), .D(ALU_A), .nEN(1'b0), .Val(A));
  DebugShift32 debugshift32_2 (.CLK(BUS_CLK), .D(ALU_B), .nEN(1'b0), .Val(B));
  DebugShift32 debugshift32_3 (.CLK(BUS_CLK), .D(ADDR_IN), .nEN(1'b0), .Val(Result));
  Reset reset_1 (.out(nRESET));
  Reset #(.invertOutput("false")) reset_2 (.out(RESET));
  Multiplexer multiplexer_2 (.sel(in_11), .in_0(ADDR_IN), .in_1(MEPC_OUT), .out(PC_IN));
  Multiplexer multiplexer_3 (.sel(OP_IN_MUX), .in_0(MEM_OUT), .in_1(IRQ_OP), .out(OP_IN));
  D_FF d_ff_2 (.D(OP_LATCH), .C(CLK), .Q(OP_IMM_LATCH));  // open: nQ
  Multiplexer #(.Selector_Bits(2)) multiplexer_4 (
    .sel(ALU_A_MUX), .in_0(RS1), .in_1(PC_OUT), .in_2(1'b1), .in_3(1'b0), .out(ALU_A));
  D_FF d_ff_3 (.D(ALU_AUX), .C(CLK), .Q(d_ff_3_q));  // open: nQ
  not not_2 (nPC_CNT_PE, PC_IN_LATCH);
  Comparator #(.Bits(12)) comparator_2 (.a(CSR_Address), .b(12'h340), .eq(comparator_2_eq));  // open: gt, lt
  Clock_driver clock_driver_1 (
    .CLK_RAW(CLK_RAW), .Stop(B_STOP), .Run(B_RUN), .One_Instruction(B_INSTR), .One_Step(B_STEP),
    .One_Substep(B_SUBSTEP), .nSTEPDONE(nSTEPDONE), .nOPDONE(nOPDONE), .nRESET(nRESET), .CLK(CLK),
    .nCLK(nCLK), .Running(Running));
  or or_1 (or_1_out, nSTEPDONE, d_ff_3_q);
  nand nand_2 (LEN8, LEN[0], BUS_EN);
  ALU_shift_step alu_shift_step_1 (
    .nCLK(nCLK), .nRESET(nALU_RESET), .nEN(or_1_out), .SH_LOADLEN(alu_shift_step_1_sh_loadlen),
    .nSH_OUTPUT(alu_shift_step_1_nsh_output), .SH_RESET(alu_shift_step_1_sh_reset));
  // PC pc_1: pin names not known; wires that end beside it: CLK, BUS_CLK, PC_IN, PC_IN_LATCH, LASTSTEP, PC_OUT_SnP, nPC_CNT_PE, OP_LATCH, nRESET, PC_OUT, PC
  // OpCode opcode_1: pin names not known; wires that end beside it: BUS_CLK, OP_IN, OP_LATCH, OP_IMM_LATCH, BUS_EN, nRESET, ImmI, ImmS, ImmB, ImmU, ImmJ, ImmCSR, RSA, RSB, RSD, out_12[10:6], out_12[13:11], out_12[14], nS_EXT, out_12[16], opcode_1_p21, Instr, out_13
  Multiplexer #(.Selector_Bits(3)) multiplexer_5 (
    .sel(ALU_B_MUX), .in_0(MEM_IN), .in_1(ImmI), .in_2(ImmS), .in_3(ImmB), .in_4(ImmU), .in_5(ImmJ),
    .in_6(1'b1), .in_7(1'b0), .out(ALU_B));
  HEF4557B hef4557b_1 (
    .DA(CSR_OUT), .DB(hef4557b_1_q), .A_nB(comparator_2_eq), .nCP1(CSR_IN_LATCH), .CP0(BUS_CLK), .MR(RESET),
    .L32(1'b0), .L16(1'b1), .L8(1'b1), .L4(1'b1), .L2(1'b1), .L1(1'b1), .VCC(1'b1), .GND(1'b0),
    .Q(hef4557b_1_q));  // open: nQ
  nor nor_1 (LASTSTEP, LEN[0], BUS_EN);
  assign CSR_IN = comparator_2_eq ? hef4557b_1_q : 1'bz;  // Driver driver_1
  Clock clock_1 (
    .CLK(CLK), .nCLK(nCLK), .nLEN4(LEN8), .LASTSTEP(LASTSTEP), .SUBSTEP_EN(nRESET), .STEP(out_12[5:0]),
    .LASTSUBSTEP(clock_1_lastsubstep), .nSTEPDONE(nSTEPDONE), .SUBSTEP(Substep), .nOPDONE(nOPDONE));  // open: nRESET
  ALU alu_1 (
    .CLK(BUS_CLK), .A(ALU_A), .B(ALU_B), .N(ALU_N), .nRESET_ALU(nALU_RESET), .CLK_F(ALU_AUX), .S(ALU_OP),
    .LOADLEN_SH(alu_shift_step_1_sh_loadlen), .nOUTPUT_SH(alu_shift_step_1_nsh_output),
    .RESET_SH(alu_shift_step_1_sh_reset));  // open: FLAG, OUT, DLEN, DSUM
  Multiplexer #(.Selector_Bits(2)) multiplexer_6 (
    .sel(REG_IN_MUX), .in_0(ADDR_IN), .in_1(MEM_OUT), .in_2(CSR_IN), .in_3(PC_OUT), .out(REG_IN));
  and and_3 (BUS_CLK, CLK, BUS_EN);
  // Mem mem_1: pin names not known; wires that end beside it: CLK, BUS_CLK, MEM_IN, ADDR_IN, ADDR_LATCH, ADDR_CLK, nADDR_PE, nMEM_OE, nMEM_WE, nRESET, ROM_DATA, nS_EXT, MEM_OUT, ADDR, Dout, Dval, ROM_ADDR, ROM_SEL, ROM_DIN
  // Register_bank register_bank_1: pin names not known; wires that end beside it: BUS_CLK, REG_IN, nREG_IN_EN, RSA, RSB, RSD, RESET, RS1, MEM_IN
  ROM #(.AddrBits(17), .isProgramMemory("true"), .Bits(32)) MicroCode (
    .A(out_12), .sel(1'b1),
    .D({MicroCode_d, CSR_IN_LATCH, CSR_OUT_LATCH, CSR_ADDR_LATCH, OP_LATCH, REG_IN_MUX, ALU_B_MUX, ALU_A_MUX, nMEM_WE, nMEM_OE, nADDR_PE, ADDR_CLK, ADDR_LATCH, PC_OUT_SnP, PC_IN_LATCH, nREG_IN_EN, BUS_EN, LEN[0], ALU_OP, ALU_AUX, nALU_RESET, ALU_N}));
  EEPROM #(.AddrBits(16), .Bits(8)) Firmware (.A(ROM_ADDR), .CS(ROM_SEL), .WE(~nMEM_WE), .OE(~nMEM_OE), .D(ROM_DATA));
  assign ROM_DATA = ~nMEM_WE ? ROM_DIN : 8'bz;  // DriverInvSel driverinvsel_1

  assign Step = out_12[5:0];

  // Other names for the same wires on the sheet: IMM_SnP = BUS_EN; LEN[1] = BUS_EN; PC_CNT_EN = OP_LATCH;
  //   ALU_OUT = ADDR_IN; CSR_ADDR[11:0] = CSR_Address; FLAG = out_12[15]; FUNC3[2:0] = out_12[13:11];
  //   gp[31:0] = x3_gp; Mem_Dout[7:0] = Dout; Mem_Dval[7:0] = Dval; OPCODE[4:0] = out_12[10:6]; PC_IN_MUX = in_11;
  //   PC_OUT_LATCH = LASTSTEP; RS2 = MEM_IN; SA = out_12[14]; SYS = out_12[16]

  // Notes on the sheet:
  //   CLK_RAW: Hz: 5000
  //   Debug
  //   Interrupts
  //   CSR
  //   Clock
  //   ALU
  //   PC
  //   Opcode
  //   Registers
  //   Memory
  //   Microcode
  //   ROM
  //   contents of MicroCode (hex, n*v repeats v):
  //   1d1c0a8a,190202,130202,1d0242,170202,1d0242,170202,1d0242,170202,1d0242,3d0202,1d0200,
  //   41c0282,190202,130202,201d0042,201d0042,201d0042,201d0042,201d0102,0,0,0,0,0,0,0,
  //   0,0,0,0,0,1d1c0a8a,190202,130202,1d0242,170202,1d0242,170202,1d0242,170202,1d0242,
  //   3d0202,3d0202,3d0202,3d0302,0,0,0,0,0,0,0,0,0,0,0,0,0,0,0,0,0,0,1d1c0a8a,190202,130202,
  //   1d0242,170202,1d0242,170202,1d0242,170202,1d0242,3d0202,3d0202,3d0202,3d0302,0,0,
  //   0,0,0,0,0,0,0,0,0,0,0,0,0,0,0,0,1d1c0a8a,190202,130202,1d0242,170202,1d0242,170202,
  //   1d0242,170202,1d0242,3d0202,3d0202,3d0202,3d0302,0,0,0,0,0,0,0,0,0,0,0,0,0,0,0,0,
  //   0,0,1d1c0a8a,190202,130202,1d0242,170202,1d0242,170202,1d0242,170202,1d0242,3d0202,
  //   1d0200,41d0082,1d0302,0,0,0,0,0,0,0,0,0,0,0,0,0,0,0,0,0,0,1d1c0a8a,190202,130202,
  //   1d0242,170202,1d0242,170202,1d0242,170202,1d0242,3d0202,1d0200,111d0882,1d0302,0,
  //   0,0,0,0,0,0,0,0,0,0,0,0,0,0,0,0,0,1d1c0a8a,190202,130202,1d0242,170202,1d0242,170202,
  //   1d0242,170202,1d0242,3d0202,3d0202,3d0202,3d0302,0,0,0,0,0,0,0,0,0,0,0,0,0,0,0,0,
  //   0,0,1d1c0a8a,190202,130202,1d0242,170202,1d0242,170202,1d0242,170202,1d0242,3d0202,
  //   3d0202,3d0202,3d0302,0,0,0,0,0,0,0,0,0,0,0,0,0,0,0,0,0,0,1d1c0a8a,190202,130202,1d0242,
  //   170202,1d0242,170202,1d0242,170202,1d0242,3d0202,1d0200,81c0282,190202,1a0242,c0202,
  //   1c0302,0,0,0,0,0,0,0,0,0,0,0,0,0,0,0,1d1c0a8a,190202,130202,1d0242,170202,1d0242,
  //   170202,1d0242,170202,1d0242,3d0202,3d0202,3d0202,3d0302,0,0,0,0,0,0,0,0,0,0,0,0,0,
  //   0,0,0,0,0,1d1c0a8a,190202,130202,1d0242,170202,1d0242,170202,1d0242,170202,1d0242,
  //   3d0202,3d0202,3d0202,3d0302,0,0,0,0,0,0,0,0,0,0,0,0,0,0,0,0,0,0,1d1c0a8a,190202,130202,
  //   1d0242,170202,1d0242,170202,1d0242,170202,1d0242,3d0202,3d0202,3d0202,3d0302,0,0,
  //   0,0,0,0,0,0,0,0,0,0,0,0,0,0,0,0,1d1c0a8a,190202,130202,1d0242,170202,1d0242,170202,
  //   1d0242,170202,1d0242,3d0202,1d0200,1d0082,1d0302,0,0,0,0,0,0,0,0,0,0,0,0,0,0,0,0,
  //   0,0,1d1c0a8a,190202,130202,1d0242,170202,1d0242,170202,1d0242,170202,1d0242,3d0202,
  //   1d0200,131d0082,1d0302,0,0,0,0,0,0,0,0,0,0,0,0,0,0,0,0,0,0,1d1c0a8a,190202,130202,
  //   1d0242,170202,1d0242,170202,1d0242,170202,1d0242,3d0202,3d0202,3d0202,3d0302,0,0,
  //   0,0,0,0,0,0,0,0,0,0,0,0,0,0,0,0,1d1c0a8a,190202,130202,1d0242,170202,1d0242,170202,
  //   1d0242,170202,1d0242,3d0202,3d0202,3d0202,3d0302,0,0,0,0,0,0,0,0,0,0,0,0,0,0,0,0,
  //   0,0,1d1c0a8a,190202,130202,1d0242,170202,1d0242,170202,1d0242,170202,1d0242,3d0202,
  //   3d0202,3d0202,3d0302,0,0,0,0,0,0,0,0,0,0,0,0,0,0,0,0,0,0,1d1c0a8a,190202,130202,1d0242,
  //   170202,1d0242,170202,1d0242,170202,1d0242,3d0202,3d0202,3d0202,3d0302,0,0,0,0,0,0,
  //   0,0,0,0,0,0,0,0,0,0,0,0,1d1c0a8a,190202,130202,1d0242,170202,1d0242,170202,1d0242,
  //   170202,1d0242,3d0202,3d0202,3d0202,3d0302,0,0,0,0,0,0,0,0,0,0,0,0,0,0,0,0,0,0,1d1c0a8a,
  //   190202,130202,1d0242,170202,1d0242,170202,1d0242,170202,1d0242,3d0202,3d0202,3d0202,
  //   3d0302,0,0,0,0,0,0,0,0,0,0,0,0,0,0,0,0,0,0,1d1c0a8a,190202,130202,1d0242,170202,1d0242,
  //   170202,1d0242,170202,1d0242,3d0202,3d0202,3d0202,3d0302,0,0,0,0,0,0,0,0,0,0,0,0,0,
  //   0,0,0,0,0,1d1c0a8a,190202,130202,1d0242,170202,1d0242,170202,1d0242,170202,1d0242,
  //   3d0202,3d0202,3d0202,3d0302,0,0,0,0,0,0,0,0,0,0,0,0,0,0,0,0,0,0,1d1c0a8a,190202,130202,
  //   1d0242,170202,1d0242,170202,1d0242,170202,1d0242,3d0202,3d0202,3d0202,3d0302,0,0,
  //   0,0,0,0,0,0,0,0,0,0,0,0,0,0,0,0,1d1c0a8a,190202,130202,1d0242,170202,1d0242,170202,
  //   1d0242,170202,1d0242,3d0202,3d0202,3d0202,3d0302,0,0,0,0,0,0,0,0,0,0,0,0,0,0,0,0,
  //   0,0,1d1c0a8a,190202,130202,1d0242,170202,1d0242,170202,1d0242,170202,1d0242,3d0202,
  //   1d0201,1d0293,1d0206,1d0302,0,0,0,0,0,0,0,0,0,0,0,0,0,0,0,0,0,1d1c0a8a,190202,130202,
  //   1d0242,170202,1d0242,170202,1d0242,170202,1d0242,3d0202,1d0200,41d0282,1d0600,1d1d08c2,
  //   1d1d0202,191d08c2,191d08c2,191d08c2,191d0842,191d0842,191d0842,1d0302,0,0,0,0,0,0,
  //   0,0,0,1d1c0a8a,190202,130202,1d0242,170202,1d0242,170202,1d0242,170202,1d0242,3d0202,
  //   3d0202,3d0202,3d0302,0,0,0,0,0,0,0,0,0,0,0,0,0,0,0,0,0,0,1d1c0a8a,190202,130202,1d0242,
  //   170202,1d0242,170202,1d0242,170202,1d0242,3d0202,1d0200,151d0a82,1d0600,1d1d08c2,
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  //   contents of Firmware (hex, n*v repeats v):
  //   13,4,70,2,93,6,f0,6,17,15,0,0,3,15,85,ff,97,15,0,0,83,95,25,ff,13,0,0,0,13,0,0,0,
  //   13,0,0,0,13,0,0,0,13,0,0,0,13,0,0,0,13,0,0,0,13,0,0,0,13,0,0,0,13,0,0,0,97,2,0,0,
  //   23,9a,a2,0,97,2,0,0,23,97,b2,0,f,10,0,0,93,86,d6,14,13,0,0,0,93,3,c0,1b,93,4,20,0,
  //   63,9c,76,6,13,7,40,6,13,7,f7,ff,e3,1e,7,fe,97,2,0,0,23,96,a2,4,97,2,0,0,23,93,b2,
  //   4,f,10,0,0,13,0,0,0,13,0,0,0,13,0,0,0,13,0,0,0,13,0,0,0,13,0,0,0,13,0,0,0,13,0,0,
  //   0,13,0,0,0,13,0,0,0,13,0,0,0,13,0,0,0,13,0,0,0,13,0,0,0,93,86,d6,14,13,0,0,0,93,3,
  //   90,30,93,4,30,0,63,96,76,0,63,4,90,0,6f,0,40,1,63,80,4,0,93,10,4,1,b3,81,90,0,6f,
  //   0,0,0,13,4,80,2,73,55,0,34,73,d5,7,34,93,3,0,0,93,4,f0,0,63,12,75,c,73,10,0,34,73,
  //   25,0,34,93,3,0,0,93,4,0,1,63,18,75,a,73,d0,1,34,73,25,0,34,93,3,30,0,93,4,20,0,63,
  //   1e,75,8,f3,f5,0,34,93,3,30,0,93,4,30,0,63,96,75,8,73,66,2,34,93,3,20,0,93,4,40,0,
  //   63,1e,76,6,f3,56,1,34,93,3,60,0,93,4,50,0,63,96,76,6,37,25,ad,b,13,5,a5,de,f3,15,
  //   5,34,93,3,20,0,93,4,60,0,63,9a,75,4,37,25,0,0,13,5,a5,de,73,35,5,34,b7,23,ad,b,93,
  //   83,a3,de,93,4,70,0,63,1c,75,2,37,c5,0,0,13,5,f5,ee,73,25,5,34,b7,3,ad,b,93,4,80,0,
  //   63,10,75,2,73,25,0,34,b7,c3,ad,b,93,83,f3,ee,93,4,90,0,63,16,75,0,63,4,90,0,6f,0,
  //   40,1,63,80,4,0,93,10,4,1,b3,81,90,0,6f,0,0,0,93,1,10,0,6f,0,0,0,0,0,0,0,0,0,0,0,0,
  //   0,0,0,0,0,0,0,0,0,0,0,0,0,0,0,0,0,0,0,0,0,0,0,0,0,0,0,0,0,0,0,0,0,0,0,0,0,0,0,0,0,
  //   0,0,0,0,0,0,0,0,0,0,0,0,0,0,0,0,0,0,0,0,0,0,0,0,0,0,0,0,0,0,0,0,0,0,0,0,0,0,0,0,0,
  //   0,0,0,0,0,0,0,0,0,0,0,0,0,0,0,0,0,0,0,0,0,0,0,0,0,0,0,0,0,0,0,0,0,0,0,0,0,0,0,0,0,
  //   0,0,0,0,0,0,0,0,0,0,0,0,0,0,0,0,0,0,0,0,0,0,0,0,0,0,0,0,0,0,0,0,0,0,0,0,0,0,0,0,0,
  //   0,0,0,0,0,0,0,0,0,0,0,0,0,0,0,0,0,0,0,0,0,0,0,0,0,0,0,0,0,0,0,0,0,0,0,0,0,0,0,0,0,
  //   0,0,0,0,0,0,0,0,0,0,0,0,0,0,0,0,0,0,0,0,0,0,0,0,0,0,0,0,0,0,0,0,0,0,0,0,0,0,0,0,0,
  //   0,0,0,0,0,0,0,0,0,0,0,0,0,0,0,0,0,0,0,0,0,0,0,0,0,0,0,0,0,0,0,0,0,0,0,0,0,0,0,0,0,
  //   0,0,0,0,0,0,0,0,0,0,0,0,0,0,0,0,0,0,0,0,0,0,0,0,0,0,0,0,0,0,0,0,0,0,0,0,0,0,0,0,0,
  //   0,0,0,0,0,0,0,0,0,0,0,0,0,0,0,0,0,0,0,0,0,0,0,0,0,0,0,0,0,0,0,0,0,0,0,0,0,0,0,0,0,
  //   0,0,0,0,0,0,0,0,0,0,0,0,0,0,0,0,0,0,0,0,0,0,0,0,0,0,0,0,0,0,0,0,0,0,0,0,0,0,0,0,0,
  //   0,0,0,0,0,0,0,0,0,0,0,0,0,0,0,0,0,0,0,0,0,0,0,0,0,0,0,0,0,0,0,0,0,0,0,0,0,0,0,0,0,
  //   0,0,0,0,0,0,0,0,0,0,0,0,0,0,0,0,0,0,0,0,0,0,0,0,0,0,0,0,0,0,0,0,0,0,0,0,0,0,0,0,0,
  //   0,0,0,0,0,0,0,0,0,0,0,0,0,0,0,0,0,0,0,0,0,0,0,0,0,0,0,0,0,0,0,0,0,0,0,0,0,0,0,0,0,
  //   0,0,0,0,0,0,0,0,0,0,0,0,0,0,0,0,0,0,0,0,0,0,0,0,0,0,0,0,0,0,0,0,0,0,0,0,0,0,0,0,0,
  //   0,0,0,0,0,0,0,0,0,0,0,0,0,0,0,0,0,0,0,0,0,0,0,0,0,0,0,0,0,0,0,0,0,0,0,0,0,0,0,0,0,
  //   0,0,0,0,0,0,0,0,0,0,0,0,0,0,0,0,0,0,0,0,0,0,0,0,0,0,0,0,0,0,0,0,0,0,0,0,0,0,0,0,0,
  //   0,0,0,0,0,0,0,0,0,0,0,0,0,0,0,0,0,0,0,0,0,0,0,0,0,0,0,0,0,0,0,0,0,0,0,0,0,0,0,0,0,
  //   0,0,0,0,0,0,0,0,0,0,0,0,0,0,0,0,0,0,0,0,0,0,0,0,0,0,0,0,0,0,0,0,0,0,0,0,0,0,0,0,0,
  //   0,0,0,0,0,0,0,0,0,0,0,0,0,0,0,0,0,0,0,0,0,0,0,0,0,0,0,0,0,0,0,0,0,0,0,0,0,0,0,0,0,
  //   0,0,0,0,0,0,0,0,0,0,0,0,0,0,0,0,0,0,0,0,0,0,0,0,0,0,0,0,0,0,0,0,0,0,0,0,0,0,0,0,0,
  //   0,0,0,0,0,0,0,0,0,0,0,0,0,0,0,0,0,0,0,0,0,0,0,0,0,0,0,0,0,0,0,0,0,0,0,0,0,0,0,0,0,
  //   0,0,0,0,0,0,0,0,0,0,0,0,0,0,0,0,0,0,0,0,0,0,0,0,0,0,0,0,0,0,0,0,0,0,0,0,0,0,0,0,0,
  //   0,0,0,0,0,0,0,0,0,0,0,0,0,0,0,0,0,0,0,0,0,0,0,0,0,0,0,0,0,0,0,0,0,0,0,0,0,0,0,0,0,
  //   0,0,0,0,0,0,0,0,0,0,0,0,0,0,0,0,0,0,0,0,0,0,0,0,0,0,0,0,0,0,0,0,0,0,0,0,0,0,0,0,0,
  //   0,0,0,0,0,0,0,0,0,0,0,0,0,0,0,0,0,0,0,0,0,0,0,0,0,0,0,0,0,0,0,0,0,0,0,0,0,0,0,0,0,
  //   0,0,0,0,0,0,0,0,0,0,0,0,0,0,0,0,0,0,0,0,0,0,0,0,0,0,0,0,0,0,0,0,0,0,0,0,0,0,0,0,0,
  //   0,0,0,0,0,0,0,0,0,0,0,0,0,0,0,0,0,0,0,0,0,0,0,0,0,0,0,0,0,0,0,0,0,0,0,0,0,0,0,0,0,
  //   0,0,0,0,0,0,0,0,0,0,0,0,0,0,0,0,0,0,0,0,0,0,0,0,0,0,0,0,0,0,0,0,0,0,0,0,0,0,0,0,0,
  //   0,0,0,0,0,0,0,0,0,0,0,0,0,0,0,0,0,0,0,0,0,0,0,0,0,0,0,0,0,0,0,0,0,0,0,0,0,0,0,0,0,
  //   0,0,0,0,0,0,0,0,0,0,0,0,0,0,0,0,0,0,0,0,0,0,0,0,0,0,0,0,0,0,0,0,0,0,0,0,0,0,0,0,0,
  //   0,0,0,0,0,0,0,0,0,0,0,0,0,0,0,0,0,0,0,0,0,0,0,0,0,0,0,0,0,0,0,0,0,0,0,0,0,0,0,0,0,
  //   0,0,0,0,0,0,0,0,0,0,0,0,0,0,0,0,0,0,0,0,0,0,0,0,0,0,0,0,0,0,0,0,0,0,0,0,0,0,0,0,0,
  //   0,0,0,0,0,0,0,0,0,0,0,0,0,0,0,0,0,0,0,0,0,0,0,0,0,0,0,0,0,0,0,0,0,0,0,0,0,0,0,0,0,
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endmodule
